# Fritzing sketch LogicalAudioSelector (saved by Fritzing 0.9.2b)
breadboards: 1

parts:
  RG1 = RELAY [package=relay-t9a]
  R1 = RELAY [package=relay-t9a]
  L1 = RELAY [package=relay-t9a]
  R2 = RELAY [package=relay-t9a]
  L2 = RELAY [package=relay-t9a]
  LG2 = RELAY [package=relay-t9a]
  Pie_In = Audio Jack Breakout
  Aux = Audio Jack Breakout
  Radio_In = Audio Jack Breakout
  Left = SPEAKER [package=pcb_mount_speaker]
  Right = SPEAKER [package=pcb_mount_speaker]
  Subwoofer = SPEAKER [package=pcb_mount_speaker]
  LF_Channel = Mono 2.5W Class D Audio Amplifier - PAM8302
  Right_Channel = Mono 2.5W Class D Audio Amplifier - PAM8302
  Left_Channel = Mono 2.5W Class D Audio Amplifier - PAM8302
  Radio_Power = SWITCH-SPST-2 [package=switch-spst-vertical]
  T1 = RELAY [package=relay-t9a]
  T2 = RELAY [package=relay-t9a]
  Audio = SWITCH-DPDT [package=eg2211]
  Internet = Toggle Switch [package=THT]
  EdgeRouter = LOAD
  POE = LOAD
  Unifi = LOAD
  12V-5V_USB = LOAD
  RPi = LOAD
  RG2 = RELAY [package=relay-t9a]
  RG2_2 = RELAY [package=relay-t9a]
  T3 = RELAY [package=relay-t9a]
  T4 = RELAY [package=relay-t9a]
  12V_LED_Light_Switch = SWITCH-SPST-2 [package=switch-spst-vertical]
  light2 = LOAD
  light1 = LOAD

nets:
  GND: RG1.COIL1, R1.COIL1, L1.COIL1, R2.COIL1, L2.COIL1, LG2.COIL1, LF_Channel.GND, Right_Channel.GND, Left_Channel.GND, T1.COIL1, T2.COIL1, EdgeRouter.Pin_1, Unifi.Pin_1, RPi.Pin_1, RG2.COIL1, RG2_2.COIL1, T3.COIL2, T4.COIL1, light2.Pin_1, light1.Pin_1
  N1: RG1.COIL2, R1.COIL2, L1.COIL2, T1.COIL2, Audio.3, RG2.COIL2
  N2: RG1.MAIN, LG2.NC
  N3: RG1.NC, Radio_In.GND
  N4: RG1.NO, Aux.GND, RG2.NO
  N5: R1.MAIN, R2.NC
  N6: R1.NC, Radio_In.RING
  N7: R1.NO, Aux.RING
  N8: L1.MAIN, L2.NC
  N9: L1.NC, Radio_In.TIP
  N10: L1.NO, Aux.TIP
  N11: R2.COIL2, L2.COIL2, LG2.COIL2, T2.COIL2, Audio.4, RG2_2.COIL2
  N12: R2.MAIN, LF_Channel.AIN+, Right_Channel.AIN+
  N13: R2.NO, Pie_In.RING
  N14: L2.MAIN, Left_Channel.AIN+
  N15: L2.NO, Pie_In.TIP
  N16: LG2.MAIN, Left_Channel.AIN-
  N17: LG2.NO, Pie_In.GND, RG2_2.NO
  N18: Radio_In.RING_SHUNT, RG2.NC
  N19: Left.+, Left_Channel.VO+
  N20: Left.-, Left_Channel.VO-
  N21: Right.+, Right_Channel.VO+
  N22: Right.-, Right_Channel.VO-
  N23: Subwoofer.+, LF_Channel.VO+
  N24: Subwoofer.-, LF_Channel.VO-
  VCC: LF_Channel.VCC, Right_Channel.VCC, Left_Channel.VCC
  N25: LF_Channel.AIN-, Right_Channel.AIN-, RG2_2.MAIN
  N26: Radio_Power.O, T3.COIL1
  12V: Radio_Power.P, T1.NO, T2.NO, Audio.2, Internet.COM, T3.NO, 12V_LED_Light_Switch.P
  N27: T1.MAIN, T2.MAIN, T3.MAIN
  N28: Audio.1, T4.NC
  N29: Audio.5, Internet.L1, EdgeRouter.Pin_0, POE.Pin_0, 12V-5V_USB.Pin_0, T4.COIL2
  N30: POE.Pin_1, Unifi.Pin_0
  N31: 12V-5V_USB.Pin_1, RPi.Pin_0
  N32: RG2.MAIN, RG2_2.NC
  N33: 12V_LED_Light_Switch.O, light2.Pin_0, light1.Pin_0

notes:
  Audio: 3 Position ON-OFF-ON DPDT Switch
  T4: Turns On Aux if Internet is Off if switch is in Down Position
  T1: Aux Amp Trigger (Triggers in "Down or Up if Interent is Off)
  T2: RPi Amp Trigger (only triggers if Internet is On)
  T3: Radio Trigger
  Audio Switch Position ON DOWN: Auxiliary
  Audio Switch Position OFF CENTER: Radio
  Audio Switch Position ON UP:
  IF INTERNET IS ON: Raspberry Pi
  IF INTERNET IS OFF: Auxiliary
  3 Channel Audio Amplifier to Speakers and Subwoofer, Only On When an Audio Source is Triggered

custom parts:
  Mono 2.5W Class D Audio Amplifier - PAM8302: A super small but powerful mono amplifier able to deliver up to 2.5 Watts into 4-8 ohm impedance speakers. Inside the miniature chip is a class D controller, able to run from 2.0V-5.5VDC. Since the amp is a class D, its very efficient (over 90% efficient when driving an 8Ω speaker at over half a Watt) - making it perfect for portable and battery-powered projects.
  LOAD: A generic resistor (0.25W)
